// Logisim project UAL.circ as structural Verilog: 2 circuits, main circuit main
module main (
  input  L_C,
  input  B0,
  input  A0,
  input  B1,
  input  A1,
  input  B2,
  input  A2,
  input  B3,
  input  A3,
  output Z0,
  output Z1,
  output Z2,
  output Z3,
  output Z,
  output S,
  output C,
  output V
);

  wire and_1_out, and_2_out, suma_1_carry_out, suma_2_carry_out, suma_3_carry_out, suma_4_carry_out,
       xor_1_out, xor_2_out, xor_3_out, xor_4_out;

  xor xor_1 (xor_1_out, B0, L_C);
  xor xor_2 (xor_2_out, B1, L_C);
  xor xor_3 (xor_3_out, B2, L_C);
  xor xor_4 (xor_4_out, B3, L_C);
  suma suma_1 (.Input1(xor_1_out), .Input2(A0), .Carry_in(L_C), .Carry_out(suma_1_carry_out), .Sum(Z0));
  suma suma_2 (.Input1(xor_2_out), .Input2(A1), .Carry_in(suma_1_carry_out), .Carry_out(suma_2_carry_out), .Sum(Z1));
  suma suma_3 (.Input1(xor_3_out), .Input2(A2), .Carry_in(suma_2_carry_out), .Carry_out(suma_3_carry_out), .Sum(Z2));
  suma suma_4 (.Input1(xor_4_out), .Input2(A3), .Carry_in(suma_3_carry_out), .Carry_out(suma_4_carry_out), .Sum(S));
  xor xor_5 (C, suma_4_carry_out, L_C);
  and and_1 (and_1_out, ~A3, ~xor_4_out, S);  // AND_Gate
  and and_2 (and_2_out, A3, xor_4_out, ~S);  // AND_Gate
  and and_3 (Z, ~Z0, ~Z1, ~Z2, ~S);  // AND_Gate
  or or_1 (V, and_1_out, and_2_out);

  assign Z3 = S;
endmodule

module suma (
  input  Carry_in,
  input  Input1,
  input  Input2,
  output Sum,
  output Carry_out
);

  wire AND_2_out, AND_out, XOR_out;

  xor XOR (XOR_out, Input1, Input2);
  and AND (AND_out, Carry_in, XOR_out);
  and AND_2 (AND_2_out, Input2, Input1);
  xor XOR_2 (Sum, XOR_out, Carry_in);
  or OR (Carry_out, AND_out, AND_2_out);
endmodule
