// Logisim project multiplicador-2-bits.circ as structural Verilog: 1 circuit, main circuit main
module main (
  input  A1,
  input  A0,
  input  B0,
  input  B1
);

  wire and_1_out, and_2_out, and_3_out, and_4_out, and_5_out, and_6_out, and_7_out, and_8_out, and_9_out,
       or_1_out, or_2_out, or_3_out;

  and and_1 (and_1_out, ~A1, A0, ~B0, B1);  // AND_Gate
  and and_2 (and_2_out, ~A1, A0, B0, ~B1);  // AND_Gate
  and and_3 (and_3_out, ~A1, A0, B0, B1);  // AND_Gate
  and and_4 (and_4_out, A1, ~A0, ~B0, B1);  // AND_Gate
  and and_5 (and_5_out, A1, ~A0, B0, ~B1);  // AND_Gate
  and and_6 (and_6_out, A1, ~A0, B0, B1);  // AND_Gate
  and and_7 (and_7_out, A1, A0, ~B0, B1);  // AND_Gate
  and and_8 (and_8_out, A1, A0, B0, ~B1);  // AND_Gate
  and and_9 (and_9_out, A1, A0, B0, B1);
  or or_1 (or_1_out, and_5_out, and_6_out, and_8_out);
  or or_2 (or_2_out, and_2_out, and_3_out, and_4_out, and_6_out, and_7_out, and_8_out);
  or or_3 (or_3_out, and_1_out, and_3_out, and_7_out, and_9_out);
  LED Z3 (.in(and_9_out));
  LED Z2 (.in(or_1_out));
  LED Z1 (.in(or_2_out));
  LED Z0 (.in(or_3_out));
endmodule
